// Logisim project Circuit.circ as structural Verilog: 1 circuit, main circuit main
module main (
  input  [8:0] Address_to_Write_Operand,
  input  W_prime_R,
  input  Manual_Write_Default_Load,
  input  [15:0] Operand_Data_to_insert,
  input  [3:0] Address_to_Write_Instruction,
  input  [15:0] Insert_Instruction,
  input  Manual_Write_Default_Load_2,
  input  W_prime_R_2,
  input  Initialize_PC,
  output [15:0] Operation_Output,
  output [3:0] OP_Code,
  output Overflow,
  output [15:0] Higher_Carry,
  output [15:0] out_14,
  output [3:0] OP_Code_2,
  output [15:0] Remainder,
  output [2:0] Register_Select
);

  wire comparator_1_eq, comparator_2_eq, comparator_3_eq, comparator_4_eq, comparator_5_eq, comparator_6_eq,
       comparator_7_eq, decoder_1_out0, decoder_1_out1, decoder_1_out2, decoder_1_out3, decoder_1_out4,
       decoder_1_out5, decoder_1_out6, decoder_1_out7, Main_Clock_out, multiplexer_5_out, multiplexer_6_out,
       not_1_out, not_2_out, not_3_out, not_5_out, or_1_out, PC_Clock_out;
  wire [3:0] adder_1_out, multiplexer_1_out, PC_q, register_1_q;
  wire [8:0] multiplexer_2_out;
  wire [15:0] adder_2_out, adder_3_out, and_1_out, demultiplexer_1_out1, demultiplexer_1_out2,
       demultiplexer_1_out3, demultiplexer_1_out4, demultiplexer_1_out5, demultiplexer_1_out6,
       demultiplexer_1_out7, demultiplexer_1_out8, demultiplexer_1_out9, demultiplexer_1_out10,
       demultiplexer_1_out11, demultiplexer_1_out12, demultiplexer_1_out13, demultiplexer_1_out14,
       demultiplexer_1_out15, demultiplexer_2_out0, demultiplexer_2_out2, demultiplexer_2_out3,
       demultiplexer_2_out4, demultiplexer_2_out5, demultiplexer_2_out8, demultiplexer_2_out9,
       demultiplexer_2_out11, demultiplexer_2_out12, demultiplexer_2_out13, demultiplexer_2_out14,
       demultiplexer_2_out15, divider_1_out, Memory_Exchange_Buffer_q, multiplexer_3_out, multiplexer_4_out,
       multiplexer_7_out, multiplier_1_out, not_4_out, or_2_out, R0_q, R1_q, R2_q, R3_q, R4_q, R5_q, R6_q,
       R7_q, ram_1_data, ram_2_data, Register_Exchange_Buffer_q, shifter_1_out, shifter_2_out, shifter_3_out,
       shifter_4_out, subtractor_1_out, subtractor_2_out;

  Comparator #(.width(4)) comparator_1 (.a(4'b1011), .b(OP_Code), .eq(comparator_1_eq));  // open: gt, lt
  Multiplexer #(.width(4), .enable("false")) multiplexer_1 (
    .in0(Address_to_Write_Instruction), .in1(PC_q), .out(multiplexer_1_out), .sel(Manual_Write_Default_Load_2));
  Clock PC_Clock (.out(PC_Clock_out));
  Clock Main_Clock (.out(Main_Clock_out));
  Comparator #(.width(4)) comparator_2 (.a(4'b0001), .b(OP_Code), .eq(comparator_2_eq));  // open: gt, lt
  not not_1 (not_1_out, W_prime_R_2);
  Comparator #(.width(1)) comparator_3 (.a(comparator_1_eq), .b(1'b1), .eq(comparator_3_eq));  // open: gt, lt
  Comparator #(.width(1)) comparator_4 (.a(comparator_2_eq), .b(1'b1), .eq(comparator_4_eq));  // open: gt, lt
  RAM #(.addrWidth(4), .dataWidth(16), .bus("separate")) ram_1 (
    .addr(multiplexer_1_out), .din(Insert_Instruction), .data(ram_1_data), .str(not_1_out),
    .clk(Main_Clock_out), .ld(W_prime_R_2));  // open: sel, clr
  Adder #(.width(4)) adder_1 (.a(PC_q), .b(4'b0001), .out(adder_1_out));  // open: cin, cout
  Multiplexer #(.width(9), .enable("false")) multiplexer_2 (
    .in0(Address_to_Write_Operand), .in1(out_14[15:7]), .out(multiplexer_2_out),
    .sel(Manual_Write_Default_Load));
  not not_2 (not_2_out, comparator_4_eq);
  Register #(.width(4)) PC (.D(adder_1_out), .Q(PC_q), .clk(PC_Clock_out), .clr(Initialize_PC));  // open: en
  Multiplexer #(.width(16), .enable("false")) multiplexer_3 (
    .in0(Operand_Data_to_insert), .in1(multiplexer_4_out), .out(multiplexer_3_out),
    .sel(Manual_Write_Default_Load));
  Multiplexer #(.width(16), .enable("false")) multiplexer_4 (
    .in0(demultiplexer_1_out1), .in1(Register_Exchange_Buffer_q), .out(multiplexer_4_out),
    .sel(multiplexer_5_out));
  Multiplexer #(.enable("false")) multiplexer_5 (
    .in0(comparator_3_eq), .in1(not_2_out), .out(multiplexer_5_out), .sel(comparator_4_eq));
  Register #(.width(16)) IR (.D(ram_1_data), .Q({out_14[15:4], OP_Code}), .clk(Main_Clock_out));  // open: en, clr
  not not_3 (not_3_out, multiplexer_6_out);
  RAM #(.addrWidth(9), .dataWidth(16), .bus("separate")) ram_2 (
    .addr(multiplexer_2_out), .din(multiplexer_3_out), .data(ram_2_data), .str(not_3_out),
    .clk(Main_Clock_out), .ld(multiplexer_6_out));  // open: sel, clr
  Multiplexer #(.enable("false")) multiplexer_6 (.in0(W_prime_R), .in1(1'b0), .out(multiplexer_6_out), .sel(or_1_out));
  Register #(.width(4)) register_1 (.D(OP_Code), .Q(register_1_q), .clk(Main_Clock_out));  // open: en, clr
  or or_1 (or_1_out, comparator_5_eq, comparator_6_eq);
  Comparator #(.width(4)) comparator_5 (.a(4'b1011), .b(register_1_q), .eq(comparator_5_eq));  // open: gt, lt
  Comparator #(.width(4)) comparator_6 (.a(4'b0001), .b(OP_Code), .eq(comparator_6_eq));  // open: gt, lt
  Decoder #(.select(3), .enable("false")) decoder_1 (
    .out0(decoder_1_out0), .out1(decoder_1_out1), .out2(decoder_1_out2), .out3(decoder_1_out3),
    .out4(decoder_1_out4), .out5(decoder_1_out5), .out6(decoder_1_out6), .out7(decoder_1_out7),
    .sel(out_14[6:4]));
  Register #(.width(16)) R0 (.D(Operation_Output), .en(decoder_1_out0), .Q(R0_q), .clk(Main_Clock_out));  // open: clr
  Register #(.width(16)) R1 (.D(Operation_Output), .en(decoder_1_out1), .Q(R1_q), .clk(Main_Clock_out));  // open: clr
  Register #(.width(16)) R2 (.D(Operation_Output), .en(decoder_1_out2), .Q(R2_q), .clk(Main_Clock_out));  // open: clr
  Register #(.width(16)) R3 (.D(Operation_Output), .en(decoder_1_out3), .Q(R3_q), .clk(Main_Clock_out));  // open: clr
  Register #(.width(16)) R4 (.D(Operation_Output), .en(decoder_1_out4), .Q(R4_q), .clk(Main_Clock_out));  // open: clr
  Register #(.width(16)) R5 (.D(Operation_Output), .en(decoder_1_out5), .Q(R5_q), .clk(Main_Clock_out));  // open: clr
  Register #(.width(16)) R6 (.D(Operation_Output), .en(decoder_1_out6), .Q(R6_q), .clk(Main_Clock_out));  // open: clr
  Register #(.width(16)) R7 (.D(Operation_Output), .en(decoder_1_out7), .Q(R7_q), .clk(Main_Clock_out));  // open: clr
  Multiplexer #(.select(3), .width(16), .enable("false")) multiplexer_7 (
    .in0(R0_q), .in1(R1_q), .in2(R2_q), .in3(R3_q), .in4(R4_q), .in5(R5_q), .in6(R6_q), .in7(R7_q),
    .out(multiplexer_7_out), .sel(out_14[6:4]));
  Multiplexer #(.select(4), .width(16), .enable("false")) multiplexer_8 (
    .in0(demultiplexer_2_out0), .in2(adder_2_out), .in3(subtractor_1_out), .in4(multiplier_1_out),
    .in5(divider_1_out), .in6(adder_3_out), .in7(subtractor_2_out), .in8(and_1_out), .in9(or_2_out),
    .in10(not_4_out), .in11(Memory_Exchange_Buffer_q), .in12(shifter_1_out), .in13(shifter_2_out),
    .in14(shifter_3_out), .in15(shifter_4_out), .out(Operation_Output), .sel(OP_Code));  // open: in1
  Demultiplexer #(.select(4), .width(16), .tristate("true"), .enable("false")) demultiplexer_1 (
    .out1(demultiplexer_1_out1), .out2(demultiplexer_1_out2), .out3(demultiplexer_1_out3),
    .out4(demultiplexer_1_out4), .out5(demultiplexer_1_out5), .out6(demultiplexer_1_out6),
    .out7(demultiplexer_1_out7), .out8(demultiplexer_1_out8), .out9(demultiplexer_1_out9),
    .out10(demultiplexer_1_out10), .out11(demultiplexer_1_out11), .out12(demultiplexer_1_out12),
    .out13(demultiplexer_1_out13), .out14(demultiplexer_1_out14), .out15(demultiplexer_1_out15),
    .in(multiplexer_7_out), .sel(OP_Code));  // open: out0
  Demultiplexer #(.select(4), .width(16), .tristate("true"), .enable("false")) demultiplexer_2 (
    .out0(demultiplexer_2_out0), .out2(demultiplexer_2_out2), .out3(demultiplexer_2_out3),
    .out4(demultiplexer_2_out4), .out5(demultiplexer_2_out5), .out8(demultiplexer_2_out8),
    .out9(demultiplexer_2_out9), .out11(demultiplexer_2_out11), .out12(demultiplexer_2_out12),
    .out13(demultiplexer_2_out13), .out14(demultiplexer_2_out14), .out15(demultiplexer_2_out15),
    .in(ram_2_data), .sel(OP_Code));  // open: out1, out6, out7, out10
  Adder #(.width(16)) adder_2 (
    .a(demultiplexer_1_out2), .b(demultiplexer_2_out2), .out(adder_2_out), .cout(Overflow));  // open: cin
  Subtractor #(.width(16)) subtractor_1 (
    .a(demultiplexer_1_out3), .b(demultiplexer_2_out3), .out(subtractor_1_out));  // open: bin, bout
  Multiplier #(.width(16)) multiplier_1 (
    .a(demultiplexer_1_out4), .b(demultiplexer_2_out4), .out(multiplier_1_out), .cout(Higher_Carry));  // open: cin
  Divider #(.width(16)) divider_1 (
    .a(demultiplexer_1_out5), .b(demultiplexer_2_out5), .out(divider_1_out), .rem(Remainder));  // open: upper
  Adder #(.width(16)) adder_3 (.a(demultiplexer_1_out6), .b(16'h1), .out(adder_3_out));  // open: cin, cout
  Subtractor #(.width(16)) subtractor_2 (
    .a(demultiplexer_1_out7), .b(16'h1), .out(subtractor_2_out));  // open: bin, bout
  assign and_1_out = demultiplexer_1_out8 & demultiplexer_2_out8;  // AND_Gate and_1, 16 bits wide
  assign or_2_out = demultiplexer_1_out9 | demultiplexer_2_out9;  // OR_Gate or_2, 16 bits wide
  assign not_4_out = ~demultiplexer_1_out10;  // NOT_Gate not_4, 16 bits wide
  Shifter #(.width(16), .shift("lr")) shifter_1 (
    .in(demultiplexer_1_out12), .\dist (demultiplexer_2_out12[3:0]), .out(shifter_1_out));
  Shifter #(.width(16)) shifter_2 (
    .in(demultiplexer_1_out13), .\dist (demultiplexer_2_out13[3:0]), .out(shifter_2_out));
  Shifter #(.width(16), .shift("rr")) shifter_3 (
    .in(demultiplexer_1_out14), .\dist (demultiplexer_2_out14[3:0]), .out(shifter_3_out));
  Shifter #(.width(16), .shift("rl")) shifter_4 (
    .in(demultiplexer_1_out15), .\dist (demultiplexer_2_out15[3:0]), .out(shifter_4_out));
  Register #(.width(16)) Register_Exchange_Buffer (
    .D(demultiplexer_1_out11), .Q(Register_Exchange_Buffer_q), .clk(Main_Clock_out), .clr(not_5_out));  // open: en
  not not_5 (not_5_out, comparator_7_eq);
  Comparator #(.width(4)) comparator_7 (.a(4'b1011), .b(OP_Code), .eq(comparator_7_eq));  // open: gt, lt
  Register #(.width(16)) Memory_Exchange_Buffer (
    .D(demultiplexer_2_out11), .Q(Memory_Exchange_Buffer_q), .clk(Main_Clock_out), .clr(not_5_out));  // open: en

  assign OP_Code_2 = OP_Code;
  assign out_14[3:0] = OP_Code;
  assign Register_Select = out_14[6:4];

  // Notes on the sheet:
  //   0- Write/Store Data Manually (Initial)
  //   1- Give Control to Processor
  //   -->
  //   Opcode
  //   b(Hex)=1011(Binary)
  //   -->
  //   STORE/XCH Control
  //   <--
  //   Instruction Memory
  //   <--
  //   Memory Address
  //   Operand/Data Memory
  //   Register Sel.
  //   ^
  //   ||
  //   OP Code
  //   Read/Write Control
  //   Register File
  //   From
  //   Register
  //   From
  //   Memory
  //   Register DMX
  //   Memory DMX
  //   Substraction
  //   Division
  //   Increment
  //   Decrement
  //   Bitwise OR
  //   Bitwise NOT
  //   Right Shift
  //   Left Shift
  //   Rotate Right
  //   Rotate Left
  //   Addition
  //   Multiplication
  //   Bitwise AND
  //   b(Hex)=1011(Binary)
  //   Activates Buffer only While Exchange
endmodule
